# Fritzing sketch thingpin-wiring (saved by Fritzing 0.9.2b)

parts:
  Raspberry_Pi1 = Raspberry Pi B+
  S1 = Reed switch [package=THT]

nets:
  N1: Raspberry_Pi1.GPIO21, S1.pin_2
  N2: Raspberry_Pi1.GND, S1.pin_1
